// Logisim project Exemplo_0702.circ as structural Verilog: 1 circuit, main circuit main
module main (
  input  in_1,
  input  in_2,
  input  seletor,
  output out_4
);

  wire and_1_out, and_2_out, nor_1_out, not_1_out, or_1_out;

  or or_1 (or_1_out, in_1, in_2);
  nor nor_1 (nor_1_out, in_1, in_2);
  not not_1 (not_1_out, seletor);
  and and_1 (and_1_out, or_1_out, not_1_out);
  and and_2 (and_2_out, nor_1_out, seletor);
  or or_2 (out_4, and_1_out, and_2_out);

  // Notes on the sheet:
  //   0 --> or
  //   1 --> nor
endmodule
