// Logisim project Exemplo_0705.circ as structural Verilog: 1 circuit, main circuit main
module main (
  input  x,
  input  y,
  input  in_3,
  input  seletor_2,
  input  in_5,
  output out_6
);

  wire and_1_out, and_2_out, and_3_out, and_4_out, and_5_out, and_6_out, and_7_out, and_8_out, and_9_out,
       and_10_out, and_11_out, and_12_out, and_13_out, nand_1_out, nor_1_out, not_1_out, not_2_out,
       not_3_out, not_4_out, not_5_out, not_6_out, not_7_out, or_1_out, or_2_out, or_3_out, or_4_out,
       or_5_out, or_6_out, xnor_1_out, xor_1_out;

  not not_1 (not_1_out, x);
  or or_1 (or_1_out, x, y);
  nor nor_1 (nor_1_out, x, y);
  and and_1 (and_1_out, x, y);
  nand nand_1 (nand_1_out, x, y);
  xor xor_1 (xor_1_out, x, y);
  xnor xnor_1 (xnor_1_out, x, y);
  not not_2 (not_2_out, in_3);
  not not_3 (not_3_out, in_3);
  not not_4 (not_4_out, in_3);
  and and_2 (and_2_out, not_1_out, not_2_out);
  and and_3 (and_3_out, or_1_out, in_3);
  and and_4 (and_4_out, nor_1_out, not_3_out);
  and and_5 (and_5_out, and_1_out, in_3);
  and and_6 (and_6_out, nand_1_out, not_4_out);
  and and_7 (and_7_out, xor_1_out, in_3);
  or or_2 (or_2_out, and_2_out, and_3_out);
  or or_3 (or_3_out, and_4_out, and_5_out);
  or or_4 (or_4_out, and_6_out, and_7_out);
  not not_5 (not_5_out, seletor_2);
  not not_6 (not_6_out, seletor_2);
  and and_8 (and_8_out, or_2_out, not_5_out);
  and and_9 (and_9_out, or_3_out, seletor_2);
  and and_10 (and_10_out, or_4_out, not_6_out);
  and and_11 (and_11_out, xnor_1_out, seletor_2);
  or or_5 (or_5_out, and_8_out, and_9_out);
  or or_6 (or_6_out, and_10_out, and_11_out);
  not not_7 (not_7_out, in_5);
  and and_12 (and_12_out, or_5_out, not_7_out);
  and and_13 (and_13_out, or_6_out, in_5);
  or or_7 (out_6, and_12_out, and_13_out);

  // Notes on the sheet:
  //   000 --> not
  //   001 --> nand
  //   010 --> nor
  //   100 --> or
  //   101 --> xor
  //   110 --> and
  //   111 --> xnor
endmodule
