// Logisim project Exemplo_0503.circ as structural Verilog: 1 circuit, main circuit main
module main (
  input  a___b,
  input  in_2,
  output out_3
);

  wire nand_1_out;

  nand nand_1 (nand_1_out, a___b, in_2);
  nand nand_2 (out_3, nand_1_out, nand_1_out);
endmodule
