// Logisim project Exemplo_0508.circ as structural Verilog: 1 circuit, main circuit main
module main (
  input  a,
  input  b,
  output out_3
);

  wire nor_1_out, nor_2_out;

  nor nor_1 (nor_1_out, a, nor_2_out);
  nor nor_2 (nor_2_out, b, b);
  nor nor_3 (out_3, nor_1_out, nor_1_out);

  // Notes on the sheet:
  //   (a + ~b)
endmodule
