// Logisim project Exemplo_0509.circ as structural Verilog: 1 circuit, main circuit main
module main (
  input  a,
  input  b,
  output out_3
);

  nand nand_1 (out_3, a, b);

  // Notes on the sheet:
  //   (~a + ~b)
endmodule
