// Logisim project Exemplo_0701.circ as structural Verilog: 1 circuit, main circuit main
module main (
  input  in_1,
  input  in_2,
  input  seletor,
  output out_4
);

  wire and_1_out, and_2_out, and_3_out, nand_1_out, not_1_out;

  and and_1 (and_1_out, in_1, in_2);
  nand nand_1 (nand_1_out, in_1, in_2);
  not not_1 (not_1_out, seletor);
  and and_2 (and_2_out, and_1_out, not_1_out);
  and and_3 (and_3_out, nand_1_out, seletor);
  or or_1 (out_4, and_2_out, and_3_out);

  // Notes on the sheet:
  //   0 --> and
  //   1 --> nand
endmodule
