// Logisim project Exemplo_0704.circ as structural Verilog: 1 circuit, main circuit main
module main (
  input  x,
  input  y,
  input  seletor_1,
  input  seletor_2,
  output out_5
);

  wire and_1_out, and_2_out, and_3_out, and_4_out, and_5_out, and_6_out, nor_1_out, not_1_out, not_2_out,
       not_3_out, or_1_out, or_2_out, or_3_out, xnor_1_out, xor_1_out;

  or or_1 (or_1_out, x, y);
  xor xor_1 (xor_1_out, x, y);
  nor nor_1 (nor_1_out, x, y);
  xnor xnor_1 (xnor_1_out, x, y);
  not not_1 (not_1_out, seletor_1);
  not not_2 (not_2_out, seletor_1);
  and and_1 (and_1_out, or_1_out, not_1_out);
  and and_2 (and_2_out, xor_1_out, seletor_1);
  and and_3 (and_3_out, nor_1_out, not_2_out);
  and and_4 (and_4_out, xnor_1_out, seletor_1);
  or or_2 (or_2_out, and_1_out, and_2_out);
  or or_3 (or_3_out, and_3_out, and_4_out);
  not not_3 (not_3_out, seletor_2);
  and and_5 (and_5_out, or_2_out, not_3_out);
  and and_6 (and_6_out, or_3_out, seletor_2);
  or or_4 (out_5, and_5_out, and_6_out);

  // Notes on the sheet:
  //   00 --> nor
  //   01 --> nor
  //   01 --> xor
  //   11 --> xnor
endmodule
