// Logisim project Exemplo_0801.circ as structural Verilog: 2 circuits, main circuit main
module main (
  input  in_1,
  input  in_2,
  input  in_3,
  input  in_4,
  input  in_5,
  input  in_6,
  input  in_7,
  input  in_8,
  output out_9,
  output out_10,
  output out_11,
  output out_12
);

  wire somadorcompleto_2_vai_um, somadorcompleto_3_vai_um, somadorcompleto_4_vai_um;

  somadorCompleto somadorcompleto_1 (
    .in_1(in_1), .in_2(in_5), .in_3(somadorcompleto_2_vai_um), .soma(out_9));  // open: vai_um
  somadorCompleto somadorcompleto_2 (
    .in_1(in_2), .in_2(in_6), .in_3(somadorcompleto_3_vai_um), .soma(out_10),
    .vai_um(somadorcompleto_2_vai_um));
  somadorCompleto somadorcompleto_3 (
    .in_1(in_3), .in_2(in_7), .in_3(somadorcompleto_4_vai_um), .soma(out_11),
    .vai_um(somadorcompleto_3_vai_um));
  somadorCompleto somadorcompleto_4 (
    .in_1(in_4), .in_2(in_8), .in_3(1'b0), .soma(out_12), .vai_um(somadorcompleto_4_vai_um));

  // Notes on the sheet:
  //   X
  //   Y
endmodule

module somadorCompleto (
  input  in_1,
  input  in_2,
  input  in_3,
  output soma,
  output vai_um
);

  wire and_1_out, and_2_out, and_3_out, and_4_out, and_5_out, and_6_out, and_7_out, and_8_out, not_1_out,
       not_2_out, not_3_out, or_1_out, or_3_out, or_4_out, or_6_out;

  not not_1 (not_1_out, in_1);
  not not_2 (not_2_out, in_2);
  not not_3 (not_3_out, in_3);
  and and_1 (and_1_out, not_1_out, not_2_out, in_3);
  and and_2 (and_2_out, not_1_out, in_2, not_3_out);
  and and_3 (and_3_out, in_1, not_2_out, not_3_out);
  and and_4 (and_4_out, in_1, in_2, in_3);
  and and_5 (and_5_out, not_1_out, in_2, in_3);
  and and_6 (and_6_out, in_1, not_2_out, in_3);
  and and_7 (and_7_out, in_1, in_2, not_3_out);
  and and_8 (and_8_out, in_1, in_2, in_3);
  or or_1 (or_1_out, and_1_out, and_2_out);
  or or_2 (soma, or_1_out, or_3_out);
  or or_3 (or_3_out, and_3_out, and_4_out);
  or or_4 (or_4_out, and_5_out, and_6_out);
  or or_5 (vai_um, or_4_out, or_6_out);
  or or_6 (or_6_out, and_7_out, and_8_out);
endmodule
