// Logisim project Exemplo_0802.circ as structural Verilog: 2 circuits, main circuit main
module main (
  input  [4:0] b,
  input  [4:0] a,
  output [4:0] out_3
);

  wire subtrator_completo_2_out_5, subtrator_completo_3_out_5, subtrator_completo_4_out_5,
       subtrator_completo_5_out_5;

  subtrator_completo subtrator_completo_1 (
    .a(a[4]), .b(b[4]), .bI(subtrator_completo_2_out_5), .out_4(out_3[4]));  // open: out_5
  subtrator_completo subtrator_completo_2 (
    .a(a[3]), .b(b[3]), .bI(subtrator_completo_3_out_5), .out_4(out_3[3]), .out_5(subtrator_completo_2_out_5));
  subtrator_completo subtrator_completo_3 (
    .a(a[2]), .b(b[2]), .bI(subtrator_completo_4_out_5), .out_4(out_3[2]), .out_5(subtrator_completo_3_out_5));
  subtrator_completo subtrator_completo_4 (
    .a(a[1]), .b(b[1]), .bI(subtrator_completo_5_out_5), .out_4(out_3[1]), .out_5(subtrator_completo_4_out_5));
  subtrator_completo subtrator_completo_5 (
    .a(a[0]), .b(b[0]), .bI(1'b0), .out_4(out_3[0]), .out_5(subtrator_completo_5_out_5));
endmodule

module subtrator_completo (
  input  a,
  input  b,
  input  bI,
  output out_4,
  output out_5
);

  wire and_1_out, and_2_out, and_3_out, not_1_out, not_2_out, xor_1_out;

  xor xor_1 (xor_1_out, a, b);
  and and_1 (and_1_out, b, bI);
  not not_1 (not_1_out, a);
  and and_2 (and_2_out, not_1_out, bI);
  not not_2 (not_2_out, a);
  and and_3 (and_3_out, not_2_out, b);
  xor xor_2 (out_4, xor_1_out, bI);
  or or_1 (out_5, and_1_out, and_2_out, and_3_out);
endmodule
