// Logisim project Exemplo_0803.circ as structural Verilog: 1 circuit, main circuit main
module main (
  input  [4:0] a,
  input  [4:0] b,
  output saida
);

  wire [4:0] xnor_1_out;

  assign xnor_1_out = ~(a ^ b);  // XNOR_Gate xnor_1, 5 bits wide
  and and_1 (saida, xnor_1_out[4], xnor_1_out[3], xnor_1_out[2], xnor_1_out[1], xnor_1_out[0]);
endmodule
