// Logisim project Exemplo_0804.circ as structural Verilog: 1 circuit, main circuit main
module main (
  input  [4:0] a,
  input  [4:0] b,
  output saida
);

  wire [4:0] xor_1_out;

  assign xor_1_out = a ^ b;  // XOR_Gate xor_1, 5 bits wide
  or or_1 (saida, xor_1_out[4], xor_1_out[3], xor_1_out[2], xor_1_out[1], xor_1_out[0]);
endmodule
