// Logisim project Exemplo_0805.circ as structural Verilog: 2 circuits, main circuit main
module main (
  input  [4:0] entrada,
  input  [4:0] complemento_2,
  output [4:0] saida
);

  wire somadorcompleto_2_vai_um, somadorcompleto_3_vai_um, somadorcompleto_4_vai_um, somadorcompleto_5_vai_um;
  wire [4:0] not_1_out;

  assign not_1_out = ~entrada;  // NOT_Gate not_1, 5 bits wide
  somadorCompleto somadorcompleto_1 (
    .in_1(not_1_out[4]), .in_2(complemento_2[4]), .in_3(somadorcompleto_2_vai_um), .soma(saida[4]));  // open: vai_um
  somadorCompleto somadorcompleto_2 (
    .in_1(not_1_out[3]), .in_2(complemento_2[3]), .in_3(somadorcompleto_3_vai_um), .soma(saida[3]),
    .vai_um(somadorcompleto_2_vai_um));
  somadorCompleto somadorcompleto_3 (
    .in_1(not_1_out[2]), .in_2(complemento_2[2]), .in_3(somadorcompleto_4_vai_um), .soma(saida[2]),
    .vai_um(somadorcompleto_3_vai_um));
  somadorCompleto somadorcompleto_4 (
    .in_1(not_1_out[1]), .in_2(complemento_2[1]), .in_3(somadorcompleto_5_vai_um), .soma(saida[1]),
    .vai_um(somadorcompleto_4_vai_um));
  somadorCompleto somadorcompleto_5 (
    .in_1(not_1_out[0]), .in_2(complemento_2[0]), .in_3(1'b0), .soma(saida[0]),
    .vai_um(somadorcompleto_5_vai_um));

  // Notes on the sheet:
  //   complemento 1
endmodule

module somadorCompleto (
  input  in_1,
  input  in_2,
  input  in_3,
  output soma,
  output vai_um
);

  wire and_1_out, and_2_out, and_3_out, and_4_out, and_5_out, and_6_out, and_7_out, and_8_out, not_1_out,
       not_2_out, not_3_out, or_1_out, or_3_out, or_4_out, or_6_out;

  not not_1 (not_1_out, in_1);
  not not_2 (not_2_out, in_2);
  not not_3 (not_3_out, in_3);
  and and_1 (and_1_out, not_1_out, not_2_out, in_3);
  and and_2 (and_2_out, not_1_out, in_2, not_3_out);
  and and_3 (and_3_out, in_1, not_2_out, not_3_out);
  and and_4 (and_4_out, in_1, in_2, in_3);
  and and_5 (and_5_out, not_1_out, in_2, in_3);
  and and_6 (and_6_out, in_1, not_2_out, in_3);
  and and_7 (and_7_out, in_1, in_2, not_3_out);
  and and_8 (and_8_out, in_1, in_2, in_3);
  or or_1 (or_1_out, and_1_out, and_2_out);
  or or_2 (soma, or_1_out, or_3_out);
  or or_3 (or_3_out, and_3_out, and_4_out);
  or or_4 (or_4_out, and_5_out, and_6_out);
  or or_5 (vai_um, or_4_out, or_6_out);
  or or_6 (or_6_out, and_7_out, and_8_out);
endmodule
