// Logisim project Exemplo_1101.circ as structural Verilog: 1 circuit, main circuit main
module main (
  input  entrada,
  input  reset,
  output out_3,
  output out_4,
  output out_5,
  output out_6,
  output saida_Moore,
  output saida_Mealy
);

  wire clock_out, not_1_out;

  Clock clock (.out(clock_out));
  D_Flip_Flop d_ff_1 (.clk(clock_out), .D(entrada), .Q(out_6), .reset(reset));  // open: Qn, preset, en
  D_Flip_Flop d_ff_2 (.clk(clock_out), .D(out_6), .Q(out_5), .reset(reset));  // open: Qn, preset, en
  D_Flip_Flop d_ff_3 (.clk(clock_out), .D(out_5), .Q(out_4), .reset(reset));  // open: Qn, preset, en
  D_Flip_Flop d_ff_4 (.clk(clock_out), .D(out_4), .Q(out_3), .reset(reset));  // open: Qn, preset, en
  not not_1 (not_1_out, out_5);
  D_Flip_Flop d_ff_5 (.clk(clock_out), .D(saida_Mealy), .Q(saida_Moore), .reset(reset));  // open: Qn, preset, en
  and and_1 (saida_Mealy, out_3, out_4, not_1_out, out_6);
  Counter counter_1 (.clk(saida_Moore), .clr(reset));  // open: load, D, count, Q, carry
  Counter counter_2 (.clk(saida_Mealy), .clr(reset));  // open: load, D, count, Q, carry

  // Notes on the sheet:
  //   contador Moore
  //   contador Mealy
endmodule
