// Logisim project Exemplo_1103.circ as structural Verilog: 1 circuit, main circuit main
module main (
  input  in_1,
  input  in_2,
  output out_3,
  output out_4,
  output out_5,
  output out_6,
  output out_7
);

  wire clock_1_out, d_ff_2_q, not_1_out, not_2_out, not_3_out, not_4_out, or_1_out;

  Clock clock_1 (.out(clock_1_out));
  not not_1 (not_1_out, clock_1_out);
  D_Flip_Flop d_ff_1 (.clk(clock_1_out), .D(in_1), .Q(out_6), .reset(or_1_out));  // open: Qn, preset, en
  or or_1 (or_1_out, in_2, d_ff_2_q);
  D_Flip_Flop d_ff_2 (.clk(not_1_out), .D(out_7), .Q(d_ff_2_q), .reset(in_2));  // open: Qn, preset, en
  D_Flip_Flop d_ff_3 (.clk(clock_1_out), .D(out_6), .Q(out_5), .reset(or_1_out));  // open: Qn, preset, en
  not not_2 (not_2_out, out_5);
  not not_3 (not_3_out, out_3);
  and and_1 (out_7, out_6, not_2_out, out_4, not_3_out);
  D_Flip_Flop d_ff_4 (.clk(clock_1_out), .D(out_5), .Q(out_4), .reset(or_1_out));  // open: Qn, preset, en
  Counter counter_1 (.count(out_7), .clk(not_4_out), .clr(in_2));  // open: load, D, Q, carry
  not not_4 (not_4_out, clock_1_out);
  D_Flip_Flop d_ff_5 (.clk(clock_1_out), .D(out_4), .Q(out_3), .reset(or_1_out));  // open: Qn, preset, en
endmodule
