// Logisim project Exercicio_07.circ as structural Verilog: 10 circuits, main circuit main
module main (
  input  w_r,
  input  [1:0] \endereço ,
  input  clock,
  input  clear,
  input  [15:0] in_5,
  output [15:0] saida
);

  Ram_4_X_16 ram_4_x_16_1 (
    .w_r(w_r), .clock(clock), .clear(clear), .\endereço (\endereço ), .saida(saida), .entrada(in_5));

  // Notes on the sheet:
  //   entrada
endmodule

module Ram (
  input  \endreço ,
  input  R_W,
  input  clk,
  input  \input ,
  input  clr,
  output out_6
);

  wire and_1_out, j_k_ff_1_q, not_1_out;

  and and_1 (and_1_out, \endreço , R_W, clk);
  not not_1 (not_1_out, \input );
  J_K_Flip_Flop j_k_ff_1 (
    .J(\input ), .clk(and_1_out), .K(not_1_out), .Q(j_k_ff_1_q), .reset(clr));  // open: Qn, preset, en
  and and_2 (out_6, \endreço , j_k_ff_1_q);
endmodule

module ram_1x4 (
  input  \endereço ,
  input  w_r,
  input  clock,
  input  clear,
  input  [3:0] entrada,
  output [3:0] saida
);

  Ram_1X2 ram_1x2_1 (
    .w_r(w_r), .clock(clock), .clear(clear), .in_1(\endereço ), .out_6(saida[3:2]), .in_5(entrada[3:2]));
  Ram_1X2 ram_1x2_2 (
    .w_r(w_r), .clock(clock), .clear(clear), .in_1(\endereço ), .out_6(saida[1:0]), .in_5(entrada[1:0]));
endmodule

module Ram_1X2 (
  input  in_1,
  input  w_r,
  input  clock,
  input  clear,
  input  [1:0] in_5,
  output [1:0] out_6
);

  Ram ram_1 (.R_W(w_r), .clk(clock), .clr(clear), .\endreço (in_1), .out_6(out_6[1]), .\input (in_5[1]));
  Ram ram_2 (.R_W(w_r), .clk(clock), .clr(clear), .\endreço (in_1), .out_6(out_6[0]), .\input (in_5[0]));
endmodule

module Ram_2_X_4 (
  input  seletor,
  input  w_r,
  input  clock,
  input  clear,
  input  [3:0] entrada,
  output [3:0] saida
);

  wire not_1_out;
  wire [3:0] ram_1x4_1_saida, ram_1x4_2_saida;

  ram_1x4 ram_1x4_1 (
    .w_r(w_r), .clock(clock), .clear(clear), .\endereço (not_1_out), .entrada(entrada),
    .saida(ram_1x4_1_saida));
  ram_1x4 ram_1x4_2 (
    .w_r(w_r), .clock(clock), .clear(clear), .\endereço (seletor), .entrada(entrada), .saida(ram_1x4_2_saida));
  not not_1 (not_1_out, seletor);
  Multiplexer #(.width(4)) multiplexer_1 (
    .in0(ram_1x4_2_saida), .in1(ram_1x4_1_saida), .out(saida), .sel(not_1_out));  // open: en
endmodule

module Ram_4_X_8 (
  input  w_r,
  input  [1:0] \endreço ,
  input  clock,
  input  clear,
  input  [7:0] entrada,
  output [7:0] saida
);

  wire and_1_out, and_2_out, and_3_out, nor_1_out, not_1_out, not_2_out;
  wire [3:0] ram_2_x_4_1_saida, ram_2_x_4_2_saida, ram_2_x_4_3_saida, ram_2_x_4_4_saida, ram_2_x_4_5_saida,
       ram_2_x_4_6_saida, ram_2_x_4_7_saida, ram_2_x_4_8_saida;

  Ram_2_X_4 ram_2_x_4_1 (
    .w_r(w_r), .clock(clock), .clear(clear), .seletor(nor_1_out), .saida(ram_2_x_4_1_saida),
    .entrada(entrada[3:0]));
  Ram_2_X_4 ram_2_x_4_2 (
    .w_r(w_r), .clock(clock), .clear(clear), .seletor(nor_1_out), .saida(ram_2_x_4_2_saida),
    .entrada(entrada[7:4]));
  Ram_2_X_4 ram_2_x_4_3 (
    .w_r(w_r), .clock(clock), .clear(clear), .seletor(and_1_out), .saida(ram_2_x_4_3_saida),
    .entrada(entrada[3:0]));
  Ram_2_X_4 ram_2_x_4_4 (
    .w_r(w_r), .clock(clock), .clear(clear), .seletor(and_1_out), .saida(ram_2_x_4_4_saida),
    .entrada(entrada[7:4]));
  Ram_2_X_4 ram_2_x_4_5 (
    .w_r(w_r), .clock(clock), .clear(clear), .seletor(and_2_out), .saida(ram_2_x_4_5_saida),
    .entrada(entrada[3:0]));
  Ram_2_X_4 ram_2_x_4_6 (
    .w_r(w_r), .clock(clock), .clear(clear), .seletor(and_2_out), .saida(ram_2_x_4_6_saida),
    .entrada(entrada[7:4]));
  Ram_2_X_4 ram_2_x_4_7 (
    .w_r(w_r), .clock(clock), .clear(clear), .seletor(and_3_out), .saida(ram_2_x_4_7_saida),
    .entrada(entrada[3:0]));
  Ram_2_X_4 ram_2_x_4_8 (
    .w_r(w_r), .clock(clock), .clear(clear), .seletor(and_3_out), .saida(ram_2_x_4_8_saida),
    .entrada(entrada[7:4]));
  nor nor_1 (nor_1_out, \endreço [0], \endreço [1]);
  and and_1 (and_1_out, \endreço [0], not_1_out);
  not not_1 (not_1_out, \endreço [1]);
  not not_2 (not_2_out, \endreço [0]);
  and and_2 (and_2_out, not_2_out, \endreço [1]);
  and and_3 (and_3_out, \endreço [0], \endreço [1]);
  Multiplexer #(.select(2), .width(8)) multiplexer_1 (
    .in0({ram_2_x_4_2_saida, ram_2_x_4_1_saida}), .in1({ram_2_x_4_4_saida, ram_2_x_4_3_saida}),
    .in2({ram_2_x_4_6_saida, ram_2_x_4_5_saida}), .in3({ram_2_x_4_8_saida, ram_2_x_4_7_saida}), .out(saida),
    .sel(\endreço ));  // open: en
endmodule

module Ram_8_X_8 (
  input  w_r,
  input  [2:0] in_2,
  input  clock,
  input  clear,
  input  [7:0] in_5,
  output [7:0] out_6
);

  wire and_1_out, and_2_out, not_1_out;
  wire [7:0] ram_4_x_8_1_saida, ram_4_x_8_2_saida;

  not not_1 (not_1_out, in_2[2]);
  and and_1 (and_1_out, w_r, not_1_out);
  Ram_4_X_8 ram_4_x_8_1 (
    .w_r(and_1_out), .clock(clock), .clear(clear), .\endreço (in_2[1:0]), .saida(ram_4_x_8_1_saida),
    .entrada(in_5));
  and and_2 (and_2_out, w_r, in_2[2]);
  Ram_4_X_8 ram_4_x_8_2 (
    .w_r(and_2_out), .clock(clock), .clear(clear), .\endreço (in_2[1:0]), .saida(ram_4_x_8_2_saida),
    .entrada(in_5));
  Multiplexer #(.width(8)) multiplexer_1 (
    .in0(ram_4_x_8_1_saida), .in1(ram_4_x_8_2_saida), .out(out_6), .sel(in_2[2]));  // open: en
endmodule

module Ram_1_X_8 (
  input  \endereço ,
  input  w_r,
  input  clock,
  input  clear,
  input  [7:0] in_5,
  output [7:0] saida
);

  Ram_1X2 ram_1x2_1 (.w_r(w_r), .clock(clock), .clear(clear), .in_1(\endereço ), .out_6(saida[1:0]), .in_5(in_5[1:0]));
  Ram_1X2 ram_1x2_2 (.w_r(w_r), .clock(clock), .clear(clear), .in_1(\endereço ), .out_6(saida[3:2]), .in_5(in_5[3:2]));
  Ram_1X2 ram_1x2_3 (.w_r(w_r), .clock(clock), .clear(clear), .in_1(\endereço ), .out_6(saida[5:4]), .in_5(in_5[5:4]));
  Ram_1X2 ram_1x2_4 (.w_r(w_r), .clock(clock), .clear(clear), .in_1(\endereço ), .out_6(saida[7:6]), .in_5(in_5[7:6]));

  // Notes on the sheet:
  //   entrada
endmodule

module Ram_4_X_16 (
  input  w_r,
  input  [1:0] \endereço ,
  input  clock,
  input  clear,
  input  [15:0] entrada,
  output [15:0] saida
);

  wire and_1_out, and_2_out, and_3_out, nor_1_out, not_1_out, not_2_out;
  wire [15:0] ram_1_x_16_1_out_6, ram_1_x_16_2_out_6, ram_1_x_16_3_out_6, ram_1_x_16_4_out_6;

  Ram_1_X_16 ram_1_x_16_1 (
    .w_r(w_r), .clock(clock), .clear(clear), .in_2(nor_1_out), .out_6(ram_1_x_16_1_out_6), .in_5(entrada));
  Ram_1_X_16 ram_1_x_16_2 (
    .w_r(w_r), .clock(clock), .clear(clear), .in_2(and_1_out), .out_6(ram_1_x_16_2_out_6), .in_5(entrada));
  Ram_1_X_16 ram_1_x_16_3 (
    .w_r(w_r), .clock(clock), .clear(clear), .in_2(and_2_out), .out_6(ram_1_x_16_3_out_6), .in_5(entrada));
  Ram_1_X_16 ram_1_x_16_4 (
    .w_r(w_r), .clock(clock), .clear(clear), .in_2(and_3_out), .out_6(ram_1_x_16_4_out_6), .in_5(entrada));
  nor nor_1 (nor_1_out, \endereço [0], \endereço [1]);
  not not_1 (not_1_out, \endereço [1]);
  and and_1 (and_1_out, not_1_out, \endereço [0]);
  and and_2 (and_2_out, \endereço [1], not_2_out);
  not not_2 (not_2_out, \endereço [0]);
  and and_3 (and_3_out, \endereço [0], \endereço [1]);
  Multiplexer #(.select(2), .width(16)) multiplexer_1 (
    .in0(ram_1_x_16_1_out_6), .in1(ram_1_x_16_2_out_6), .in2(ram_1_x_16_3_out_6), .in3(ram_1_x_16_4_out_6),
    .out(saida), .sel(\endereço ));  // open: en
endmodule

module Ram_1_X_16 (
  input  w_r,
  input  in_2,
  input  clock,
  input  clear,
  input  [15:0] in_5,
  output [15:0] out_6
);

  Ram_1_X_8 ram_1_x_8_1 (
    .w_r(w_r), .clock(clock), .clear(clear), .\endereço (in_2), .saida(out_6[7:0]), .in_5(in_5[7:0]));
  Ram_1_X_8 ram_1_x_8_2 (
    .w_r(w_r), .clock(clock), .clear(clear), .\endereço (in_2), .saida(out_6[15:8]), .in_5(in_5[15:8]));
endmodule
