// Logisim project Exercicio_03.circ as structural Verilog: 1 circuit, main circuit main
module main (
  input  _1,
  input  pulse,
  input  CRL,
  output out_4,
  output out_5,
  output out_6,
  output out_7
);

  wire j_k_ff_1_qn, j_k_ff_2_qn, j_k_ff_3_qn, nand_1_out, nand_2_out, not_1_out, not_2_out;

  J_K_Flip_Flop j_k_ff_1 (
    .J(_1), .clk(pulse), .K(_1), .Q(out_7), .Qn(j_k_ff_1_qn), .reset(nand_1_out));  // open: preset, en
  nand nand_1 (nand_1_out, CRL, nand_2_out);
  not not_1 (not_1_out, out_7);
  nand nand_2 (nand_2_out, not_1_out, out_6, not_2_out, out_4);
  not not_2 (not_2_out, out_5);
  J_K_Flip_Flop j_k_ff_2 (
    .J(_1), .clk(j_k_ff_1_qn), .K(_1), .Q(out_6), .Qn(j_k_ff_2_qn), .reset(nand_1_out));  // open: preset, en
  J_K_Flip_Flop j_k_ff_3 (
    .J(_1), .clk(j_k_ff_2_qn), .K(_1), .Q(out_5), .Qn(j_k_ff_3_qn), .reset(nand_1_out));  // open: preset, en
  J_K_Flip_Flop j_k_ff_4 (.J(_1), .clk(j_k_ff_3_qn), .K(_1), .Q(out_4), .reset(nand_1_out));  // open: Qn, preset, en
endmodule
