// Logisim project Exercicio_04.circ as structural Verilog: 1 circuit, main circuit main
module main (
  input  _1,
  input  pulse,
  output out_3,
  output out_4,
  output out_5,
  output out_6
);

  wire and_1_out, j_k_ff_1_qn, j_k_ff_2_qn, j_k_ff_3_qn, j_k_ff_4_qn, not_1_out, not_2_out, not_3_out,
       or_1_out;

  not not_1 (not_1_out, _1);
  J_K_Flip_Flop j_k_ff_1 (
    .J(_1), .clk(pulse), .K(_1), .Q(out_6), .Qn(j_k_ff_1_qn), .preset(or_1_out));  // open: en, reset
  or or_1 (or_1_out, not_1_out, and_1_out);
  not not_2 (not_2_out, j_k_ff_1_qn);
  and and_1 (and_1_out, not_2_out, j_k_ff_2_qn, not_3_out, j_k_ff_4_qn);
  not not_3 (not_3_out, j_k_ff_3_qn);
  J_K_Flip_Flop j_k_ff_2 (
    .J(_1), .clk(out_6), .K(_1), .Q(out_5), .Qn(j_k_ff_2_qn), .preset(or_1_out));  // open: en, reset
  J_K_Flip_Flop j_k_ff_3 (
    .J(_1), .clk(out_5), .K(_1), .Q(out_4), .Qn(j_k_ff_3_qn), .preset(or_1_out));  // open: en, reset
  J_K_Flip_Flop j_k_ff_4 (
    .J(_1), .clk(out_4), .K(_1), .Q(out_3), .Qn(j_k_ff_4_qn), .preset(or_1_out));  // open: en, reset
endmodule
