// Logisim project Exercicio_05.circ as structural Verilog: 1 circuit, main circuit main
module main (
  input  in_1,
  input  in_2,
  output out_3,
  output out_4,
  output out_5
);

  wire t_ff_2_qn, t_ff_3_qn;

  T_Flip_Flop t_ff_1 (.clk(t_ff_2_qn), .T(t_ff_2_qn), .Q(out_3), .reset(in_2));  // open: Qn, preset, en
  T_Flip_Flop t_ff_2 (.clk(t_ff_3_qn), .T(t_ff_3_qn), .Q(out_4), .Qn(t_ff_2_qn), .reset(in_2));  // open: preset, en
  T_Flip_Flop t_ff_3 (.clk(in_1), .T(in_1), .Q(out_5), .Qn(t_ff_3_qn), .reset(in_2));  // open: preset, en
endmodule
