// Logisim project Exercicio_07.circ as structural Verilog: 1 circuit, main circuit main
module main (
  input  in_1,
  input  in_2,
  output [5:0] out_3
);

  wire clock_1_out, j_k_ff_6_qn, not_1_out, not_2_out, not_3_out, not_4_out, not_5_out, not_6_out, or_1_out;

  Clock clock_1 (.out(clock_1_out));
  or or_1 (or_1_out, in_1, j_k_ff_6_qn);
  not not_1 (not_1_out, or_1_out);
  J_K_Flip_Flop j_k_ff_1 (
    .J(or_1_out), .clk(clock_1_out), .K(not_1_out), .Q(out_3[5]), .reset(in_2));  // open: Qn, preset, en
  J_K_Flip_Flop j_k_ff_2 (
    .J(out_3[5]), .clk(clock_1_out), .K(not_2_out), .Q(out_3[4]), .reset(in_2));  // open: Qn, preset, en
  not not_2 (not_2_out, out_3[5]);
  J_K_Flip_Flop j_k_ff_3 (
    .J(out_3[4]), .clk(clock_1_out), .K(not_3_out), .Q(out_3[3]), .reset(in_2));  // open: Qn, preset, en
  not not_3 (not_3_out, out_3[4]);
  not not_4 (not_4_out, out_3[3]);
  J_K_Flip_Flop j_k_ff_4 (
    .J(out_3[3]), .clk(clock_1_out), .K(not_4_out), .Q(out_3[2]), .reset(in_2));  // open: Qn, preset, en
  J_K_Flip_Flop j_k_ff_5 (
    .J(out_3[2]), .clk(clock_1_out), .K(not_5_out), .Q(out_3[1]), .reset(in_2));  // open: Qn, preset, en
  not not_5 (not_5_out, out_3[2]);
  not not_6 (not_6_out, out_3[1]);
  J_K_Flip_Flop j_k_ff_6 (
    .J(out_3[1]), .clk(clock_1_out), .K(not_6_out), .Q(out_3[0]), .Qn(j_k_ff_6_qn), .reset(in_2));  // open: preset, en
endmodule
