// Logisim project Exercicio_01.circ as structural Verilog: 1 circuit, main circuit main
module main (
  input  clk,
  input  in_2,
  input  clear,
  output [5:0] out_4
);

  D_Flip_Flop d_ff_1 (.clk(clk), .D(out_4[4]), .Q(out_4[5]), .reset(clear));  // open: Qn, preset, en
  D_Flip_Flop d_ff_2 (.clk(clk), .D(out_4[3]), .Q(out_4[4]), .reset(clear));  // open: Qn, preset, en
  D_Flip_Flop d_ff_3 (.clk(clk), .D(out_4[2]), .Q(out_4[3]), .reset(clear));  // open: Qn, preset, en
  D_Flip_Flop d_ff_4 (.clk(clk), .D(out_4[1]), .Q(out_4[2]), .reset(clear));  // open: Qn, preset, en
  D_Flip_Flop d_ff_5 (.clk(clk), .D(out_4[0]), .Q(out_4[1]), .reset(clear));  // open: Qn, preset, en
  D_Flip_Flop d_ff_6 (.clk(clk), .D(in_2), .Q(out_4[0]), .preset(clear));  // open: Qn, en, reset
endmodule
