// Logisim project Exercicio_03.circ as structural Verilog: 1 circuit, main circuit main
module main (
  input  in_1,
  input  in_2,
  output [5:0] out_3
);

  wire clock_1_out, or_1_out;

  Clock clock_1 (.out(clock_1_out));
  or or_1 (or_1_out, out_3[0], in_1);
  D_Flip_Flop d_ff_1 (.clk(clock_1_out), .D(or_1_out), .Q(out_3[5]), .preset(in_2));  // open: Qn, en, reset
  D_Flip_Flop d_ff_2 (.clk(clock_1_out), .D(out_3[5]), .Q(out_3[4]), .reset(in_2));  // open: Qn, preset, en
  D_Flip_Flop d_ff_3 (.clk(clock_1_out), .D(out_3[4]), .Q(out_3[3]), .reset(in_2));  // open: Qn, preset, en
  D_Flip_Flop d_ff_4 (.clk(clock_1_out), .D(out_3[3]), .Q(out_3[2]), .reset(in_2));  // open: Qn, preset, en
  D_Flip_Flop d_ff_5 (.clk(clock_1_out), .D(out_3[2]), .Q(out_3[1]), .reset(in_2));  // open: Qn, preset, en
  D_Flip_Flop d_ff_6 (.clk(clock_1_out), .D(out_3[1]), .Q(out_3[0]), .reset(in_2));  // open: Qn, preset, en
endmodule
