// Logisim project Exercicio_04.circ as structural Verilog: 1 circuit, main circuit main
module main (
  input  in_1,
  input  in_2,
  input  in_3,
  output [5:0] out_4
);

  wire d_ff_1_qn, or_1_out;

  or or_1 (or_1_out, d_ff_1_qn, in_2);
  D_Flip_Flop d_ff_1 (.clk(in_1), .D(out_4[4]), .Q(out_4[5]), .Qn(d_ff_1_qn), .reset(in_3));  // open: preset, en
  D_Flip_Flop d_ff_2 (.clk(in_1), .D(out_4[3]), .Q(out_4[4]), .reset(in_3));  // open: Qn, preset, en
  D_Flip_Flop d_ff_3 (.clk(in_1), .D(out_4[2]), .Q(out_4[3]), .reset(in_3));  // open: Qn, preset, en
  D_Flip_Flop d_ff_4 (.clk(in_1), .D(out_4[1]), .Q(out_4[2]), .reset(in_3));  // open: Qn, preset, en
  D_Flip_Flop d_ff_5 (.clk(in_1), .D(out_4[0]), .Q(out_4[1]), .reset(in_3));  // open: Qn, preset, en
  D_Flip_Flop d_ff_6 (.clk(in_1), .D(or_1_out), .Q(out_4[0]), .preset(in_3));  // open: Qn, en, reset
endmodule
