// Logisim project Exercicio_05.circ as structural Verilog: 1 circuit, main circuit main
module main (
  input  in_1,
  input  in_2,
  input  in_3,
  input  [5:0] in_4,
  output [5:0] out_5
);

  wire and_1_out, and_2_out, and_3_out, and_4_out, and_5_out, and_6_out, clock_1_out;

  Clock clock_1 (.out(clock_1_out));
  D_Flip_Flop d_ff_1 (.clk(clock_1_out), .D(in_1), .Q(out_5[5]), .preset(and_1_out), .reset(in_2));  // open: Qn, en
  and and_1 (and_1_out, in_3, in_4[5]);
  D_Flip_Flop d_ff_2 (.clk(clock_1_out), .D(out_5[5]), .Q(out_5[4]), .preset(and_2_out), .reset(in_2));  // open: Qn, en
  and and_2 (and_2_out, in_3, in_4[4]);
  D_Flip_Flop d_ff_3 (.clk(clock_1_out), .D(out_5[4]), .Q(out_5[3]), .preset(and_3_out), .reset(in_2));  // open: Qn, en
  and and_3 (and_3_out, in_3, in_4[3]);
  D_Flip_Flop d_ff_4 (.clk(clock_1_out), .D(out_5[3]), .Q(out_5[2]), .preset(and_4_out), .reset(in_2));  // open: Qn, en
  and and_4 (and_4_out, in_3, in_4[2]);
  D_Flip_Flop d_ff_5 (.clk(clock_1_out), .D(out_5[2]), .Q(out_5[1]), .preset(and_5_out), .reset(in_2));  // open: Qn, en
  and and_5 (and_5_out, in_3, in_4[1]);
  D_Flip_Flop d_ff_6 (.clk(clock_1_out), .D(out_5[1]), .Q(out_5[0]), .preset(and_6_out), .reset(in_2));  // open: Qn, en
  and and_6 (and_6_out, in_3, in_4[0]);
endmodule
